// Logisim project muxrisccore.circ as structural Verilog: 1 circuit, main circuit main
module main (
);

  wire clock_1_out, clock_2_out, clock_3_out, clock_4_out, comparator_1_eq, comparator_2_eq, comparator_3_eq,
       counter_1_q, multiplexer_3_out, or_1_out;
  wire [1:0] bitselector_1_out;
  wire [15:0] bitselector_2_out, counter_2_q, multiplexer_2_out;
  wire [63:0] multiplexer_1_out, multiplexer_4_out, ram_1_dout, register_1_q;

  Register #(.trigger("falling"), .width(64)) register_1 (
    .D(multiplexer_1_out), .en(1'b1), .clk(clock_1_out), .Q(register_1_q));  // open: clr
  Multiplexer #(.width(64)) multiplexer_1 (
    .in0(ram_1_dout), .in1({64{1'b0}}), .out(multiplexer_1_out), .sel(counter_1_q));
  Clock clock_1 (.out(clock_1_out));
  BitSelector #(.group(2), .width(64)) bitselector_1 (.in(register_1_q), .out(bitselector_1_out), .sel({5{1'b0}}));
  Comparator #(.width(2)) comparator_1 (.a(bitselector_1_out), .b(2'b00), .eq(comparator_1_eq));  // open: gt, lt
  Comparator #(.width(2)) comparator_2 (.a(bitselector_1_out), .b(2'b01), .eq(comparator_2_eq));  // open: gt, lt
  Comparator #(.width(2)) comparator_3 (.a(bitselector_1_out), .b(2'b10), .eq(comparator_3_eq));  // open: gt, lt
  Counter #(.max('h1), .width(1)) counter_1 (
    .count(comparator_2_eq), .Q(counter_1_q), .clk(clock_2_out), .clr(comparator_1_eq));  // open: load, D, carry, up
  Clock clock_2 (.out(clock_2_out));
  Register #(.trigger("falling"), .width(64)) register_2 ();  // open: D, en, clk, Q, clr
  or or_1 (or_1_out, comparator_1_eq, comparator_2_eq, comparator_3_eq);
  BitSelector #(.group(16), .width(64)) bitselector_2 (.in(ram_1_dout), .out(bitselector_2_out), .sel(2'b00));
  Clock clock_3 (.out(clock_3_out));
  Counter #(.max('hffff), .trigger("falling"), .width(16)) counter_2 (
    .load(counter_1_q), .D(bitselector_2_out), .count(or_1_out), .Q(counter_2_q), .clk(clock_3_out));  // open: carry, up, clr
  Multiplexer #(.select(2), .width(16)) multiplexer_2 (
    .in0(counter_2_q), .in1(counter_2_q), .out(multiplexer_2_out), .sel(bitselector_1_out));  // open: in2, in3
  Clock clock_4 (.out(clock_4_out));
  Multiplexer #(.select(2)) multiplexer_3 (
    .in0(1'b0), .in1(1'b0), .out(multiplexer_3_out), .sel(bitselector_1_out));  // open: in2, in3
  Multiplexer #(.select(2), .width(64)) multiplexer_4 (
    .in0({64{1'b0}}), .in1({64{1'b0}}), .out(multiplexer_4_out), .sel(bitselector_1_out));  // open: in2, in3
  RAM #(.addrWidth(16), .dataWidth(64), .enables("line"), .\type ("nonvolatile")) ram_1 (
    .addr(multiplexer_2_out), .we(multiplexer_3_out), .clk(clock_4_out), .din(multiplexer_4_out),
    .dout(ram_1_dout));
endmodule
